// Logisim project Flip Flops.circ as structural Verilog
module SRFFNAND (
  input  S,
  input  R,
  output Q,
  output Qd
);

  wire not_1_out, not_2_out;

  not not_1 (not_1_out, S);
  not not_2 (not_2_out, R);
  nand nand_1 (Q, not_1_out, not_1_out, Qd);
  nand nand_2 (Qd, Q, not_2_out);

  // Notes on the sheet:
  //   The set-reset flip flop
endmodule

module SRFFNOR (
  input  S,
  input  R,
  output Q,
  output Qd
);

  wire nor_1_out, nor_2_out;

  nor nor_1 (nor_1_out, S, nor_2_out);
  nor nor_2 (nor_2_out, nor_1_out, R);
  not not_1 (Q, nor_1_out);
  not not_2 (Qd, nor_2_out);
endmodule

module CSR (
  input  S,
  input  C,
  input  R,
  output out_4,
  output out_5
);

  wire nand_1_out, nand_2_out;

  nand nand_1 (nand_1_out, S, C);
  nand nand_2 (nand_2_out, C, R);
  nand nand_3 (out_4, nand_1_out, out_5);
  nand nand_4 (out_5, out_4, nand_2_out);
endmodule

module DFF (
  input  D,
  output Out
);

  wire clock_1_out, not_1_out;

  not not_1 (not_1_out, D);
  Clock #(.lowDuration(4)) clock_1 (.out(clock_1_out));
  LED led_1 (.in(clock_1_out));
  CSR csr_1 (.S(D), .C(clock_1_out), .R(not_1_out), .out_4(Out));  // open: out_5
endmodule
