// Logisim project Logic Gate Demo.circ as structural Verilog
module myMUX (
  input  s,
  output out_2
);

  wire A_out, and_1_out, and_2_out, B_out, not_1_out;

  Clock A (.out(A_out));
  Clock #(.highDuration(5), .lowDuration(5)) B (.out(B_out));
  not not_1 (not_1_out, s);
  and and_1 (and_1_out, A_out, not_1_out);
  and and_2 (and_2_out, B_out, s);
  or or_1 (out_2, and_1_out, and_2_out);
endmodule

module myDMUX (
  input  S,
  output A,
  output B
);

  wire clock_1_out, not_1_out;

  Clock clock_1 (.out(clock_1_out));
  not not_1 (not_1_out, S);
  and and_1 (A, clock_1_out, not_1_out);
  and and_2 (B, clock_1_out, S);
endmodule

module myNOT (
  input  in_1,
  output out_2
);

  nand nand_1 (out_2, in_1, in_1);
endmodule

module myAND (
  input  in_1,
  input  in_2,
  output out_3
);

  wire nand_1_out;

  nand nand_1 (nand_1_out, in_1, in_2);
  myNOT mynot_1 (.in_1(nand_1_out), .out_2(out_3));
endmodule

module myOR (
  input  in_1,
  input  in_2,
  output out_3
);

  wire mynot_1_out_2, mynot_2_out_2;

  myNOT mynot_1 (.in_1(in_1), .out_2(mynot_1_out_2));
  myNOT mynot_2 (.in_1(in_2), .out_2(mynot_2_out_2));
  nand nand_1 (out_3, mynot_1_out_2, mynot_2_out_2);
endmodule

module myXOR (
  input  A,
  input  B,
  output out_3
);

  wire myand_1_out_3, myand_2_out_3, mynot_1_out_2, mynot_2_out_2;

  myNOT mynot_1 (.in_1(A), .out_2(mynot_1_out_2));
  myNOT mynot_2 (.in_1(B), .out_2(mynot_2_out_2));
  myAND myand_1 (.in_1(mynot_1_out_2), .in_2(B), .out_3(myand_1_out_3));
  myAND myand_2 (.in_1(A), .in_2(mynot_2_out_2), .out_3(myand_2_out_3));
  myOR myor_1 (.in_1(myand_1_out_3), .in_2(myand_2_out_3), .out_3(out_3));
endmodule
